// Logisim project CENTRAL_PROCESSING_UNIT.circ as structural Verilog: 5 circuits, main circuit DU
module ALU (
  input  [7:0] A,
  input  [7:0] B,
  input  [2:0] OpCode,
  output [7:0] C
);

  wire [7:0] adder_1_out, adder_2_out, adder_3_out, and_1_out, or_1_out, pull_resistor_1_node,
       subtractor_1_out;

  Pull_Resistor #(.pull(1)) pull_resistor_1 (.node(pull_resistor_1_node[0]));
  Pull_Resistor pull_resistor_2 (.node(pull_resistor_1_node[7]));
  Adder adder_1 (
    .a(A), .b({{7{pull_resistor_1_node[7]}}, pull_resistor_1_node[0]}), .out(adder_1_out));  // open: cin, cout
  Adder adder_2 (
    .a(B), .b({{7{pull_resistor_1_node[7]}}, pull_resistor_1_node[0]}), .out(adder_2_out));  // open: cin, cout
  Adder adder_3 (.a(A), .b(B), .out(adder_3_out));  // open: cin, cout
  Subtractor subtractor_1 (.a(A), .b(B), .out(subtractor_1_out));  // open: bin, bout
  assign and_1_out = A & B;  // AND_Gate and_1, 8 bits wide
  assign or_1_out = A | B;  // OR_Gate or_1, 8 bits wide
  Multiplexer #(.select(3), .width(8)) multiplexer_1 (
    .in0(A), .in1(B), .in2(adder_1_out), .in3(adder_2_out), .in4(adder_3_out), .in5(subtractor_1_out),
    .in6(and_1_out), .in7(or_1_out), .out(C), .sel(OpCode));
endmodule

module CPU (
  input  BI_7,
  input  BI_6,
  input  BI_5,
  input  BI_4,
  input  BI_3,
  input  BI_2,
  input  BI_1,
  input  BI_0,
  input  RESET
);

  wire CLK_out;
  wire [1:0] cu_1_mux_out;
  wire [2:0] cu_1_alu_op_code_out;
  wire [3:0] du_1_output_bus, du_1_output_bus_2;
  wire [4:0] cu_1_up_5_bit_out, du_1_mbr_out;
  wire [7:0] du_1_memory_address_bus_external, rom_1_data;

  Clock CLK (.out(CLK_out));
  ROM rom_1 (.addr(du_1_memory_address_bus_external), .data(rom_1_data));
  CU cu_1 (
    .UP_5_BIT(du_1_mbr_out), .MPC_WE(1'b1), .CLK(CLK_out), .MIR_WE(1'b1), .RESET(RESET),
    .ALU_OP_CODE_OUT(cu_1_alu_op_code_out), .MUX_OUT(cu_1_mux_out), .UP_5_BIT_OUT(cu_1_up_5_bit_out));
  Hex_Digit_Display HX_OUT_1 (.value(du_1_output_bus_2));  // open: dp
  DU du_1 (
    .Memory_Data_Bus_Ext(rom_1_data), .Input_Bus_Ext({BI_7, BI_6, BI_5, BI_4, BI_3, BI_2, BI_1, BI_0}),
    .Register_MUX(cu_1_mux_out), .CLOCK(CLK_out), .OP_CODE_ALU(cu_1_alu_op_code_out),
    .ALU_WE(cu_1_up_5_bit_out[4]), .RESET(RESET), .A_WE(cu_1_up_5_bit_out[0]), .B_WE(cu_1_up_5_bit_out[1]),
    .MBR_WE(cu_1_up_5_bit_out[2]), .PC_WE(cu_1_up_5_bit_out[3]),
    .OUTPUT_BUS({du_1_output_bus_2, du_1_output_bus}),
    .MEMORY_ADDRESS_BUS_EXTERNAL(du_1_memory_address_bus_external), .MBR_OUT(du_1_mbr_out));
  Hex_Digit_Display HX_OUT_0 (.value(du_1_output_bus));  // open: dp

  // Notes on the sheet:
  //   contents of rom_1 (hex, n*v repeats v):
  //   0 ff ff
endmodule

// O
module DU (
  input  [7:0] Memory_Data_Bus_Ext,
  input  [7:0] Input_Bus_Ext,
  input  [1:0] Register_MUX,
  input  CLOCK,
  input  [2:0] OP_CODE_ALU,
  input  ALU_WE,
  input  RESET,
  input  A_WE,
  input  B_WE,
  input  MBR_WE,
  input  PC_WE,
  output [7:0] OUTPUT_BUS,
  output [7:0] MEMORY_ADDRESS_BUS_EXTERNAL,
  output [4:0] MBR_OUT
);

  wire [7:0] A_q, alu_1_c, B_q, multiplexer_1_out, undriven;
  wire [7:5] MBR_q;

  Register A (.D(alu_1_c), .en(A_WE), .clk(CLOCK), .Q(A_q), .clr(RESET));
  Register B (.D(alu_1_c), .en(B_WE), .clk(CLOCK), .Q(B_q), .clr(RESET));
  Register MBR (.D(undriven), .en(MBR_WE), .clk(CLOCK), .Q({MBR_q, MBR_OUT}), .clr(RESET));
  Register PC (.D(alu_1_c), .en(PC_WE), .clk(CLOCK), .Q(MEMORY_ADDRESS_BUS_EXTERNAL), .clr(RESET));
  Multiplexer #(.select(2), .width(8)) multiplexer_1 (
    .in0(B_q), .in1({MBR_q, MBR_OUT}), .in2(MEMORY_ADDRESS_BUS_EXTERNAL), .in3(Input_Bus_Ext),
    .out(multiplexer_1_out), .sel(Register_MUX));
  ALU alu_1 (.A(A_q), .B(multiplexer_1_out), .OpCode(OP_CODE_ALU), .C(alu_1_c));
  Register Ausgabe (.D(alu_1_c), .en(ALU_WE), .clk(CLOCK), .Q(OUTPUT_BUS));  // open: clr
endmodule

module CU (
  input  [4:0] UP_5_BIT,
  input  MPC_WE,
  input  CLK,
  input  MIR_WE,
  input  RESET,
  output [2:0] ALU_OP_CODE_OUT,
  output [1:0] MUX_OUT,
  output [4:0] UP_5_BIT_OUT
);

  wire [4:0] multiplexer_1_out, register_1_q;
  wire [15:0] MCS_data;
  wire [15:10] MIR_q;

  Multiplexer #(.width(5)) multiplexer_1 (.in0(UP_5_BIT), .in1(MIR_q[15:11]), .out(multiplexer_1_out), .sel(MIR_q[10]));
  Register #(.width(5)) register_1 (.D(multiplexer_1_out), .en(MPC_WE), .clk(CLK), .Q(register_1_q), .clr(RESET));
  ROM #(.addrWidth(5), .dataWidth(16)) MCS (.addr(register_1_q), .data(MCS_data));
  Register #(.width(16)) MIR (
    .D(MCS_data), .en(MIR_WE), .clk(CLK), .Q({MIR_q, ALU_OP_CODE_OUT, UP_5_BIT_OUT, MUX_OUT}), .clr(RESET));

  // Notes on the sheet:
  //   contents of MCS (hex, n*v repeats v):
  //   da2 10
endmodule

module CPU_ALL_IN_ONE (
  input  BI_7,
  input  BI_6,
  input  BI_5,
  input  BI_4,
  input  BI_3,
  input  BI_2,
  input  BI_1,
  input  BI_0,
  input  RESET
);

  wire and_1_out, and_2_out, and_3_out, and_4_out, and_5_out, and_6_out, and_7_out, CLK_out, not_1_out,
       not_2_out, not_3_out, not_4_out, or_1_out, xor_1_out, xor_2_out;
  wire [0:0] multiplexer_5_out;
  wire [3:0] Ausgabe_q, Ausgabe_q_2;
  wire [4:0] MBR_q, multiplexer_1_out, register_1_q;
  wire [7:0] A_q, alu_1_c, B_q, multiplexer_2_out, multiplexer_3_out, multiplexer_4_out, PC_q, ram_1_dout;
  wire [7:5] MBR_q_2;
  wire [15:0] MCS_data, MIR_q;

  Clock CLK (.out(CLK_out));
  Multiplexer #(.width(5)) multiplexer_1 (
    .in0(MBR_q), .in1({MIR_q[15:12], multiplexer_5_out[0]}), .out(multiplexer_1_out), .sel(MIR_q[10]));
  Register #(.width(5)) register_1 (.D(multiplexer_1_out), .en(1'b1), .clk(CLK_out), .Q(register_1_q), .clr(RESET));
  Multiplexer #(.width(8)) multiplexer_2 (.in0(PC_q), .in1({MBR_q_2, MBR_q}), .out(multiplexer_2_out), .sel(and_6_out));
  and and_1 (and_1_out, not_1_out, and_6_out);
  not not_1 (not_1_out, MIR_q[6]);
  RAM #(.\type ("nonvolatile")) ram_1 (
    .addr(multiplexer_2_out), .we(and_1_out), .oe(1'b1), .clk(CLK_out), .din(A_q), .dout(ram_1_dout));
  and and_2 (and_2_out, MIR_q[6], and_6_out);
  ROM #(.addrWidth(5), .dataWidth(16)) MCS (.addr(register_1_q), .data(MCS_data));
  Multiplexer #(.width(8)) multiplexer_3 (.in0(alu_1_c), .in1(ram_1_dout), .out(multiplexer_3_out), .sel(and_2_out));
  Register A (.D(multiplexer_3_out), .en(and_3_out), .clk(CLK_out), .Q(A_q), .clr(RESET));
  Register B (.D(alu_1_c), .en(and_5_out), .clk(CLK_out), .Q(B_q), .clr(RESET));
  Register MBR (.D(ram_1_dout), .en(xor_1_out), .clk(CLK_out), .Q({MBR_q_2, MBR_q}), .clr(RESET));
  Register PC (.D(alu_1_c), .en(xor_2_out), .clk(CLK_out), .Q(PC_q), .clr(RESET));
  Register #(.trigger("falling"), .width(16)) MIR (.D(MCS_data), .en(1'b1), .clk(CLK_out), .Q(MIR_q), .clr(RESET));
  and and_3 (and_3_out, MIR_q[2], not_4_out);
  Multiplexer #(.select(2), .width(8)) multiplexer_4 (
    .in0(B_q), .in1({MBR_q_2, MBR_q}), .in2(PC_q), .in3({BI_7, BI_6, BI_5, BI_4, BI_3, BI_2, BI_1, BI_0}),
    .out(multiplexer_4_out), .sel(MIR_q[1:0]));
  and and_4 (and_4_out, not_2_out, MIR_q[6]);
  not not_2 (not_2_out, and_6_out);
  and and_5 (and_5_out, MIR_q[3], not_4_out);
  ALU alu_1 (.A(A_q), .B(multiplexer_4_out), .OpCode(MIR_q[9:7]), .C(alu_1_c));
  or or_1 (or_1_out, A_q[0], A_q[1], A_q[2], A_q[3], A_q[4], A_q[5], A_q[6], A_q[7]);
  Multiplexer multiplexer_5 (.in0(MIR_q[11]), .in1(not_3_out), .out(multiplexer_5_out[0]), .sel(and_7_out));
  not not_3 (not_3_out, or_1_out);
  Register Ausgabe (.D(alu_1_c), .en(and_4_out), .clk(CLK_out), .Q({Ausgabe_q_2, Ausgabe_q}), .clr(RESET));
  xor xor_1 (xor_1_out, MIR_q[4], and_6_out);
  and and_6 (and_6_out, MIR_q[4], MIR_q[5]);
  xor xor_2 (xor_2_out, MIR_q[5], and_6_out);
  Hex_Digit_Display HX_OUT_1 (.value(Ausgabe_q_2));  // open: dp
  not not_4 (not_4_out, and_7_out);
  and and_7 (and_7_out, MIR_q[2], MIR_q[3]);
  Hex_Digit_Display HX_OUT_0 (.value(Ausgabe_q));  // open: dp

  // Notes on the sheet:
  //   contents of MCS (hex, n*v repeats v):
  //   da2 8410 487 25a2 3410 440 3c70 474 4da2 5410 5c00 64a1 410 75a2 7c92 485 0 504 cda2 430 408 704 784
  //   604 684 9c10 d400 e684 f40c 410 eda2 4400
endmodule
